# Fritzing sketch Panner.03 (saved by Fritzing 0.9.3b)
breadboards: 1

parts:
  Teensy_3_2 = Teensy 3.1
  TMC2100 = Pololu A4988 [package=SO16]
  J1 = screw terminal, 4 pins
  1_3"_128X64_OLED = Grove OLED 128x96
  R1 = Resistor [tolerance=±5% resistance=4.7k package=THT]
  R2 = Resistor [tolerance=±5% resistance=4.7k package=THT]
  C1 = Electrolytic Capacitor [capacitance=0.1mF voltage=20V package="300 mil [THT, electrolytic]"]
  ThumbStick = Thumb Joystick
  R3 = Resistor [tolerance=±5% resistance=22k package=THT]
  R4 = Resistor [tolerance=±5% resistance=4.7k package=THT]
  SPI_Display = LED Matrix - Serial Interface - Red/Green/Blue
  M1 = Stepper Motor - Bipolar

nets:
  GND: Teensy_3_2.GND, Teensy_3_2.AGND, TMC2100.GND, 1_3"_128X64_OLED.GND, C1.-, ThumbStick.GND, R4.Pin_1, SPI_Display.GND
  N1: Teensy_3_2.D3, TMC2100.STEP
  N2: Teensy_3_2.D6, TMC2100.DIR
  N3: Teensy_3_2.D10, SPI_Display.CS
  N4: Teensy_3_2.D11, SPI_Display.MOSI
  N5: Teensy_3_2.D12, SPI_Display.MISO
  3.3V: Teensy_3_2.3V3, TMC2100.VDD, 1_3"_128X64_OLED.VCC, R1.Pin_0, R2.Pin_0, ThumbStick.VCC, SPI_Display.VCC
  N6: Teensy_3_2.D13, SPI_Display.SCK
  N7: Teensy_3_2.A0/D14, R3.Pin_1, R4.Pin_0
  N8: Teensy_3_2.A4/D18, 1_3"_128X64_OLED.SDA, R1.Pin_1
  N9: Teensy_3_2.A5/D19, 1_3"_128X64_OLED.SCL, R2.Pin_1
  N10: Teensy_3_2.A7/D21, ThumbStick.SEL
  N11: Teensy_3_2.A8/D22, ThumbStick.VERT
  N12: Teensy_3_2.A9/D23, ThumbStick.HORZ
  5V: Teensy_3_2.Vin
  N13: TMC2100.1B, J1.pin4, M1.C
  N14: TMC2100.1A, J1.pin3, M1.A
  N15: TMC2100.2A, J1.pin2, M1.B
  N16: TMC2100.2B, J1.pin1, M1.D
  18V: TMC2100.VMOT, C1.+, R3.Pin_0
