# Fritzing sketch Panner.04 (saved by Fritzing 0.9.3b)
breadboards: 1

parts:
  Teensy_3_2 = Teensy 3.1
  TMC2100 = Pololu A4988 [package=SO16]
  M1 = Stepper Motor - Bipolar
  J1 = screw terminal, 4 pins
  C1 = Electrolytic Capacitor [capacitance=0.1mF voltage=20V package="300 mil [THT, electrolytic]"]
  R3 = Resistor [tolerance=±5% resistance=22k package=THT]
  R4 = Resistor [tolerance=±5% resistance=4.7k package=THT]
  U1 = Voltage Regulator - 5V [package="TO220 [THT]"]

nets:
  GND: Teensy_3_2.GND, Teensy_3_2.AGND, TMC2100.GND, C1.-, R4.Pin_1, U1.GND
  N1: Teensy_3_2.D3, TMC2100.STEP
  N2: Teensy_3_2.D6, TMC2100.DIR
  3.3V: Teensy_3_2.3V3, TMC2100.VDD
  N3: Teensy_3_2.A0/D14, R3.Pin_1, R4.Pin_0
  5V: Teensy_3_2.Vin, U1.output_voltage
  N4: TMC2100.1B, M1.C, J1.pin4
  N5: TMC2100.1A, M1.A, J1.pin3
  N6: TMC2100.2A, M1.B, J1.pin2
  N7: TMC2100.2B, M1.D, J1.pin1
  18V: TMC2100.VMOT, C1.+, R3.Pin_0, U1.input_voltage

notes:
  5V
  3.3V
